// Logisim project Green8bit.circ as structural Verilog: 1 circuit, main circuit main
module main (
  input  [7:0] A,
  input  [7:0] B
);

  wire and_1_out, and_2_out, and_3_out, and_4_out, and_5_out, and_6_out, and_7_out, and_8_out, and_9_out,
       and_10_out, and_11_out, and_12_out, and_13_out, and_14_out, and_15_out, and_16_out, and_17_out,
       and_18_out, and_19_out, and_20_out, and_21_out, and_22_out, and_23_out, and_24_out, and_25_out,
       and_26_out, and_27_out, and_28_out, and_29_out, and_30_out, and_31_out, and_32_out, and_33_out,
       and_34_out, and_35_out, and_36_out, and_37_out, and_38_out, and_39_out, and_40_out, and_41_out,
       and_42_out, and_43_out, and_44_out, and_45_out, and_46_out, and_47_out, and_48_out, and_49_out,
       and_50_out, and_51_out, and_52_out, and_53_out, and_54_out, and_55_out, and_56_out, not_1_out,
       not_2_out, not_3_out, not_4_out, not_5_out, not_6_out, not_7_out, not_8_out, not_9_out, not_10_out,
       not_11_out, not_12_out, not_13_out, not_14_out, not_15_out, not_16_out, not_17_out, not_18_out,
       not_19_out, not_20_out, not_21_out, not_22_out, not_23_out, not_24_out, or_2_out, or_4_out, or_6_out,
       or_8_out, or_10_out, or_12_out, or_14_out, or_16_out;
  wire [7:0] or_1_out;

  // Probe on A
  // Probe on B
  not not_1 (not_1_out, A[0]);
  not not_2 (not_2_out, B[0]);
  not not_3 (not_3_out, 1'b0);
  not not_4 (not_4_out, A[1]);
  not not_5 (not_5_out, B[1]);
  not not_6 (not_6_out, or_2_out);
  not not_7 (not_7_out, A[2]);
  not not_8 (not_8_out, B[2]);
  not not_9 (not_9_out, or_4_out);
  not not_10 (not_10_out, A[3]);
  not not_11 (not_11_out, B[3]);
  not not_12 (not_12_out, or_6_out);
  not not_13 (not_13_out, A[4]);
  not not_14 (not_14_out, B[4]);
  not not_15 (not_15_out, or_8_out);
  not not_16 (not_16_out, A[5]);
  not not_17 (not_17_out, B[5]);
  not not_18 (not_18_out, or_10_out);
  not not_19 (not_19_out, A[6]);
  not not_20 (not_20_out, B[6]);
  not not_21 (not_21_out, or_12_out);
  not not_22 (not_22_out, A[7]);
  not not_23 (not_23_out, B[7]);
  not not_24 (not_24_out, or_14_out);
  and and_1 (and_1_out, not_1_out, not_2_out, 1'b0);
  and and_2 (and_2_out, not_1_out, B[0], not_3_out);
  and and_3 (and_3_out, A[0], not_2_out, not_3_out);
  and and_4 (and_4_out, A[0], B[0], 1'b0);
  and and_5 (and_5_out, not_1_out, 1'b0);
  and and_6 (and_6_out, not_1_out, B[0]);
  and and_7 (and_7_out, B[0], 1'b0);
  and and_8 (and_8_out, not_4_out, not_5_out, or_2_out);
  and and_9 (and_9_out, not_4_out, B[1], not_6_out);
  and and_10 (and_10_out, A[1], not_5_out, not_6_out);
  and and_11 (and_11_out, A[1], B[1], or_2_out);
  and and_12 (and_12_out, not_4_out, or_2_out);
  and and_13 (and_13_out, not_4_out, B[1]);
  and and_14 (and_14_out, B[1], or_2_out);
  and and_15 (and_15_out, not_7_out, not_8_out, or_4_out);
  and and_16 (and_16_out, not_7_out, B[2], not_9_out);
  and and_17 (and_17_out, A[2], not_8_out, not_9_out);
  and and_18 (and_18_out, A[2], B[2], or_4_out);
  and and_19 (and_19_out, not_7_out, or_4_out);
  and and_20 (and_20_out, not_7_out, B[2]);
  and and_21 (and_21_out, B[2], or_4_out);
  and and_22 (and_22_out, not_10_out, not_11_out, or_6_out);
  and and_23 (and_23_out, not_10_out, B[3], not_12_out);
  and and_24 (and_24_out, A[3], not_11_out, not_12_out);
  and and_25 (and_25_out, A[3], B[3], or_6_out);
  and and_26 (and_26_out, not_10_out, or_6_out);
  and and_27 (and_27_out, not_10_out, B[3]);
  and and_28 (and_28_out, B[3], or_6_out);
  and and_29 (and_29_out, not_13_out, not_14_out, or_8_out);
  and and_30 (and_30_out, not_13_out, B[4], not_15_out);
  and and_31 (and_31_out, A[4], not_14_out, not_15_out);
  and and_32 (and_32_out, A[4], B[4], or_8_out);
  and and_33 (and_33_out, not_13_out, or_8_out);
  and and_34 (and_34_out, not_13_out, B[4]);
  and and_35 (and_35_out, B[4], or_8_out);
  and and_36 (and_36_out, not_16_out, not_17_out, or_10_out);
  and and_37 (and_37_out, not_16_out, B[5], not_18_out);
  and and_38 (and_38_out, A[5], not_17_out, not_18_out);
  and and_39 (and_39_out, A[5], B[5], or_10_out);
  and and_40 (and_40_out, not_16_out, or_10_out);
  and and_41 (and_41_out, not_16_out, B[5]);
  and and_42 (and_42_out, B[5], or_10_out);
  and and_43 (and_43_out, not_19_out, not_20_out, or_12_out);
  and and_44 (and_44_out, not_19_out, B[6], not_21_out);
  and and_45 (and_45_out, A[6], not_20_out, not_21_out);
  and and_46 (and_46_out, A[6], B[6], or_12_out);
  and and_47 (and_47_out, not_19_out, or_12_out);
  and and_48 (and_48_out, not_19_out, B[6]);
  and and_49 (and_49_out, B[6], or_12_out);
  and and_50 (and_50_out, not_22_out, not_23_out, or_14_out);
  and and_51 (and_51_out, not_22_out, B[7], not_24_out);
  and and_52 (and_52_out, A[7], not_23_out, not_24_out);
  and and_53 (and_53_out, A[7], B[7], or_14_out);
  and and_54 (and_54_out, not_22_out, or_14_out);
  and and_55 (and_55_out, not_22_out, B[7]);
  and and_56 (and_56_out, B[7], or_14_out);
  or or_1 (or_1_out[0], and_1_out, and_2_out, and_3_out, and_4_out);
  or or_2 (or_2_out, and_5_out, and_6_out, and_7_out);
  or or_3 (or_1_out[1], and_8_out, and_9_out, and_10_out, and_11_out);
  or or_4 (or_4_out, and_12_out, and_13_out, and_14_out);
  or or_5 (or_1_out[2], and_15_out, and_16_out, and_17_out, and_18_out);
  or or_6 (or_6_out, and_19_out, and_20_out, and_21_out);
  or or_7 (or_1_out[3], and_22_out, and_23_out, and_24_out, and_25_out);
  or or_8 (or_8_out, and_26_out, and_27_out, and_28_out);
  or or_9 (or_1_out[4], and_29_out, and_30_out, and_31_out, and_32_out);
  or or_10 (or_10_out, and_33_out, and_34_out, and_35_out);
  or or_11 (or_1_out[5], and_36_out, and_37_out, and_38_out, and_39_out);
  or or_12 (or_12_out, and_40_out, and_41_out, and_42_out);
  or or_13 (or_1_out[6], and_43_out, and_44_out, and_45_out, and_46_out);
  or or_14 (or_14_out, and_47_out, and_48_out, and_49_out);
  or or_15 (or_1_out[7], and_50_out, and_51_out, and_52_out, and_53_out);
  or or_16 (or_16_out, and_54_out, and_55_out, and_56_out);
  // Probe on or_1_out
  LED Overflow_Bit (.in(or_16_out));
endmodule
