// Logisim project GreenPlus5.circ as structural Verilog: 1 circuit, main circuit main
module main (
  input  [3:0] in_1,
  output [3:0] out_2,
  output Y0,
  output Y1,
  output Y2,
  output Y3
);

  wire and_1_out, and_2_out, and_3_out, and_4_out, and_5_out, and_6_out, and_7_out, and_8_out, and_9_out,
       and_10_out, and_11_out, not_1_out, not_2_out, not_3_out, not_4_out;

  // Probe on in_1
  not not_1 (not_1_out, in_1[3]);
  not not_2 (not_2_out, in_1[2]);
  not not_3 (not_3_out, in_1[1]);
  not not_4 (not_4_out, in_1[0]);
  and and_1 (and_1_out, not_1_out, in_1[2]);
  and and_2 (and_2_out, not_2_out, in_1[3], not_3_out);
  or or_1 (out_2[3], and_1_out, and_2_out, and_3_out);
  and and_3 (and_3_out, in_1[1], in_1[0], not_1_out);
  and and_4 (and_4_out, not_2_out, not_3_out);
  and and_5 (and_5_out, not_1_out, not_2_out, not_4_out);
  and and_6 (and_6_out, not_1_out, in_1[2], in_1[1], in_1[0]);
  and and_7 (and_7_out, not_1_out, not_3_out, in_1[0]);
  and and_8 (and_8_out, not_1_out, in_1[1], not_4_out);
  and and_9 (and_9_out, not_2_out, not_3_out, in_1[0]);
  and and_10 (and_10_out, not_1_out, not_4_out);
  and and_11 (and_11_out, not_2_out, not_3_out, not_4_out);
  or or_2 (out_2[2], and_4_out, and_5_out, and_6_out);
  or or_3 (out_2[1], and_7_out, and_8_out, and_9_out);
  or or_4 (out_2[0], and_10_out, and_11_out);
  // Probe on out_2

  assign Y0 = out_2[3];
  assign Y1 = out_2[2];
  assign Y2 = out_2[1];
  assign Y3 = out_2[0];
endmodule
