// Logisim project GreenTriggers.circ as structural Verilog: 1 circuit, main circuit main
module main (
);

  wire nand_1_out, nand_2_out, nand_3_out, not_1_out, not_2_out, or_1_out, v_out;
  wire [2:0] t_ff_2_q;

  Button v (.out(v_out));
  not not_1 (not_1_out, v_out);
  or or_1 (or_1_out, not_1_out, t_ff_2_q[0], t_ff_2_q[1]);
  not not_2 (not_2_out, or_1_out);
  T_Flip_Flop #(.trigger("falling")) t_ff_1 (.clk(nand_2_out), .T(1'b1), .Q(t_ff_2_q[1]));  // open: Qn, preset, reset
  T_Flip_Flop #(.trigger("falling")) t_ff_2 (.clk(v_out), .T(1'b1), .Q(t_ff_2_q[0]));  // open: Qn, preset, reset
  T_Flip_Flop #(.trigger("falling")) t_ff_3 (.clk(not_2_out), .T(1'b1), .Q(t_ff_2_q[2]));  // open: Qn, preset, reset
  // Probe on t_ff_2_q
  nand nand_1 (nand_1_out, 1'b1, t_ff_2_q[0]);
  nand nand_2 (nand_2_out, 1'b1, nand_3_out);
  nand nand_3 (nand_3_out, v_out, nand_1_out);
endmodule
